# Fritzing sketch Sketch (saved by Fritzing 0.9.3b)

parts:
  Part1 = Arduino Pro Mini (5V)
  Part2 = FTDI Basic Programmer
  Part3 = Bluetooth HC-05 Macho
  RX5808 = Barometric Pressure Sensor - BMP085 Breakout
  J1 = Piezo Speaker
  Part5 = Adafruit Micro USB Breakout [part_number="Adafruit #1833"]
  LED1 = RGB LED (com. anode, rbg) [package="5 mm [THT]"]
  LED2 = RGB LED (com. anode, rbg) [package="5 mm [THT]"]
  LED3 = RGB LED (com. anode, rbg) [package="5 mm [THT]"]
  C1 = Electrolytic Capacitor [capacitance=0.47mF package="100 mil [THT, electrolytic]"]
  C2 = Electrolytic Capacitor [capacitance=0.1mF package="100 mil [THT, electrolytic]"]  # not connected
  R1 = Resistor [tolerance=±5% resistance=100 package=THT]
  R2 = Resistor [tolerance=±5% resistance=100 package=THT]
  R3 = Resistor [tolerance=±5% resistance=100 package=THT]
  R4 = Resistor [tolerance=±5% resistance=220 package=THT]
  R5 = Resistor [tolerance=±5% resistance=220 package=THT]
  R6 = Resistor [tolerance=±5% resistance=220 package=THT]
  R7 = Resistor [tolerance=±5% resistance=220 package=THT]
  R8 = Resistor [tolerance=±5% resistance=220 package=THT]
  R9 = Resistor [tolerance=±5% resistance=220 package=THT]
  U1 = PIC-ICSP-Mini [package=pic-icsp-mini]
  U4 = PIC-ICSP-Mini [package=pic-icsp-mini]  # not connected
  U3 = PIC-ICSP-Mini [package=pic-icsp-mini]
  U2 = PIC-ICSP-Mini [package=pic-icsp-mini]
  R10 = Resistor [tolerance=±5% resistance=220 package=THT]  # not connected

nets:
  N1: Part1.DTR, Part2.DTR
  N2: Part1.TXO, Part2.RXI, Part3.RXD
  N3: Part1.RXI, Part2.TXO, Part3.TXD
  N4: Part1.VCC, Part2.POWER
  GND: Part1.GND, Part2.CTS, Part2.GND, Part5.GND, C1.-
  N5: Part1.RAW, Part3.VCC, RX5808.SCL
  N6: Part1.A3, RX5808.SDA
  N7: Part1.A2, R7.Pin_1
  N8: Part1.A1, R4.Pin_1
  N9: Part1.A0, R5.Pin_1
  N10: Part1.SCK, U1.PGC
  N11: Part1.MOSI, U1.GND
  N12: Part1.D10, U1.PGD
  N13: Part1.D9, J1.pin2
  N14: Part1.D8, R1.Pin_1
  N15: Part1.D7, R2.Pin_1
  N16: Part1.D6, R3.Pin_1
  N17: Part1.D4, R8.Pin_1
  N18: Part1.D3, R9.Pin_1
  N19: Part1.D2, R6.Pin_1
  N20: Part3.GND, RX5808.XCLR, J1.pin1
  N21: RX5808.VCC, R3.Pin_0
  N22: RX5808.GND, R2.Pin_0
  N23: RX5808.EOC, R1.Pin_0
  N24: Part5.VBUS, C1.+
  N25: LED1.common_anode, LED2.common_anode, LED3.common_anode
  N26: U3.VPP, U2.VPP
  VCC: U3.VCC, U2.VCC
  GND_2: U3.GND, U2.GND
  N27: U3.PGD, U2.PGD
  N28: U3.PGC, U2.PGC

custom parts:
  Adafruit Micro USB Breakout: Simple but effective - this breakout board has a USB Micro-B connector, with all 5 pins broken out. Great for pairing with a microcontroller with USB support, or adding USB 5V power to a project. We use a micro-AB connector with through-hole shielding pads for an excellent strong connection - it won't rip off by accident! Comes with one fully assembled and tested micro B breakout PCB and a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
